# Fritzing sketch 8Buttons (saved by Fritzing 0.9.0b)
breadboards: 1

parts:
  Bauteil1 = Arduino Uno (Rev3) - ICSP
  S1 = Square Pushbutton
  R1 = Resistor [package="2010 [SMD]"]
  R2 = Resistor [package="2010 [SMD]"]
  R3 = Resistor [package="2010 [SMD]"]
  R4 = Resistor [package="2010 [SMD]"]
  R5 = Resistor [package="2010 [SMD]"]
  R6 = Resistor [package="2010 [SMD]"]
  R7 = Resistor [package="2010 [SMD]"]
  R8 = Resistor [package="2010 [SMD]"]
  S2 = Square Pushbutton
  S3 = Square Pushbutton
  S4 = Square Pushbutton
  S5 = Square Pushbutton
  S6 = Square Pushbutton
  S7 = Square Pushbutton
  S8 = Square Pushbutton
  R9 = Rotary Potentiometer (Small) [maximum_resistance=100kΩ package=THT]

nets:
  N1: Bauteil1.A2, R9.wiper
  N2: Bauteil1.GND, R1.Pin_0, R2.Pin_0, R3.Pin_0, R4.Pin_0, R5.Pin_0, R6.Pin_0, R7.Pin_0, R8.Pin_0, R9.leg1
  N3: Bauteil1.D0/RX, S1.leg1, R1.Pin_1
  N4: Bauteil1.D1/TX, R2.Pin_1, S2.leg1
  N5: Bauteil1.D2, R3.Pin_1, S3.leg1
  N6: Bauteil1.D3_PWM, R7.Pin_1, S5.leg1
  N7: Bauteil1.D4, R6.Pin_1, S4.leg1
  N8: Bauteil1.D5_PWM, R8.Pin_1, S6.leg1
  N9: Bauteil1.D6_PWM, R4.Pin_1, S7.leg1
  N10: Bauteil1.D7, R5.Pin_1, S8.leg1
  N11: Bauteil1.5V, R9.leg2
  N12: Bauteil1.VIN, S1.leg0, S2.leg0, S3.leg0, S4.leg0, S5.leg0, S6.leg0, S7.leg0, S8.leg0
