# Fritzing sketch 8ButtonsV2 (saved by Fritzing 0.9.0b)
breadboards: 1

parts:
  R1 = Resistor [package="2010 [SMD]"]
  R2 = Resistor [package="2010 [SMD]"]
  S1 = Round Pushbutton
  S2 = Round Pushbutton
  R3 = Resistor [package="2010 [SMD]"]
  R4 = Resistor [package="2010 [SMD]"]
  S3 = Round Pushbutton
  S4 = Round Pushbutton
  Bauteil1 = Arduino Uno (Rev3)
  R5 = Resistor [package="2010 [SMD]"]
  R6 = Resistor [package="2010 [SMD]"]
  S5 = Round Pushbutton
  S6 = Round Pushbutton
  R7 = Resistor [package="2010 [SMD]"]
  R8 = Resistor [package="2010 [SMD]"]
  S7 = Round Pushbutton
  S8 = Round Pushbutton
  R9 = Rotary Potentiometer (Small) [maximum_resistance=100kΩ package=THT]

nets:
  N1: R1.Pin_0, R2.Pin_1, R3.Pin_0, R4.Pin_1, Bauteil1.GND, R5.Pin_0, R6.Pin_1, R7.Pin_0, R8.Pin_1, R9.leg1
  N2: R1.Pin_1, S2.leg1, Bauteil1.D1/TX
  N3: R2.Pin_0, S1.leg1, Bauteil1.D0/RX
  N4: S1.leg0, S2.leg0, S3.leg0, S4.leg0, Bauteil1.VIN, S5.leg0, S6.leg0, S7.leg0, S8.leg0, R9.leg2
  N5: R3.Pin_1, S4.leg1, Bauteil1.D3_PWM
  N6: R4.Pin_0, S3.leg1, Bauteil1.D2
  N7: Bauteil1.A0, R9.wiper
  N8: Bauteil1.D4, R6.Pin_0, S5.leg1
  N9: Bauteil1.D5_PWM, R5.Pin_1, S6.leg1
  N10: Bauteil1.D6_PWM, R8.Pin_0, S7.leg1
  N11: Bauteil1.D7, R7.Pin_1, S8.leg1
